# Fritzing sketch rgbkatodo (saved by Fritzing 0.9.3b)
breadboards: 1

parts:
  Part1 = iceZUM Alhambra
  LED1 = RGB LED - (4 legs) [package="5 mm [THT]"]
  R1 = Resistor [tolerance=±5% resistance=220 package=THT]
  R2 = Resistor [tolerance=±5% resistance=220 package=THT]
  R3 = Resistor [tolerance=±5% resistance=220 package=THT]

nets:
  N1: Part1.GP0, R3.Pin_1
  N2: Part1.GP1, R1.Pin_1
  N3: Part1.GP3, R2.Pin_1
  N4: Part1.GND, LED1.common_anode
  N5: LED1.red_cathode, R1.Pin_0
  N6: LED1.green_cathode, R3.Pin_0
  N7: LED1.blue_cathode, R2.Pin_0

notes:
  RGBaren 1.(gorria), 3.(berdea) eta 4. (urdina) borneei 220 Ohmeko erresistentzia konektatzen zaie seriean.
  RGBaren 2. bornea plakaren GNDra konektatuko da.
  Katodo komuneko RGBa

custom parts:
  iceZUM Alhambra: Arduino/zum compatible Open FPGA electronic board. Synthesize hardware easily, using only open source tools
